// Logisim project single cycle .risc v.circ as structural Verilog: 13 circuits, main circuit immegiate generation
module immegiate_generation (
  input  [31:0] in_1,
  input  [31:0] in_2,
  output [31:0] out_3,
  output [31:0] out_4,
  output [31:0] out_5,
  output [31:0] out_6,
  output [31:0] out_7
);

  wire [31:0] bit_extender_2_out, bit_extender_4_out, bit_extender_5_out;

  assign out_3 = {{20{in_2[31]}}, in_2[31:20]};  // Bit_Extender bit_extender_1
  assign bit_extender_2_out = {{12{in_2[31]}}, in_2[31:12]};  // Bit_Extender bit_extender_2
  assign out_4 = {{20{in_2[31]}}, {in_2[31:25], in_2[11:7]}};  // Bit_Extender bit_extender_3
  assign bit_extender_4_out = {{19{in_2[31]}}, {in_2[31], in_2[7], in_2[30:25], in_2[11:8], 1'b0}};  // Bit_Extender bit_extender_4
  assign bit_extender_5_out = {{11{in_2[31]}}, {in_2[31], in_2[19:12], in_2[20], in_2[30:21], 1'b0}};  // Bit_Extender bit_extender_5
  Adder #(.width(32)) adder_1 (.a(bit_extender_4_out), .b(in_1), .out(out_5));  // open: cin, cout
  Shifter #(.width(32)) shifter_1 (.in(bit_extender_2_out), .\dist (5'b01100), .out(out_7));
  Adder #(.width(32)) adder_2 (.a(bit_extender_5_out), .b(in_1), .out(out_6));  // open: cin, cout

  // Notes on the sheet:
  //   12 SHIFT LEFT 
  //   I TYPE
  //             S TYPE
  //            SB TYPE
  //        UJ TYPE
endmodule

module TYPE_DECODER (
  input  [6:0] in_1,
  output out_2,
  output out_3,
  output out_4,
  output out_5,
  output out_6,
  output out_7,
  output out_8,
  output out_9,
  output out_10
);

  Comparator #(.width(7)) comparator_1 (.a(in_1), .b(7'b0110011), .eq(out_2));  // open: gt, lt
  Comparator #(.width(7)) comparator_2 (.a(in_1), .b(7'b1101111), .eq(out_3));  // open: gt, lt
  Comparator #(.width(7)) comparator_3 (.a(in_1), .b(7'b0010011), .eq(out_4));  // open: gt, lt
  Comparator #(.width(7)) comparator_4 (.a(in_1), .b(7'b0000011), .eq(out_5));  // open: gt, lt
  Comparator #(.width(7)) comparator_5 (.a(in_1), .b(7'b1100111), .eq(out_6));  // open: gt, lt
  Comparator #(.width(7)) comparator_6 (.a(in_1), .b(7'b0100011), .eq(out_7));  // open: gt, lt
  Comparator #(.width(7)) comparator_7 (.a(in_1), .b(7'b1100011), .eq(out_8));  // open: gt, lt
  Comparator #(.width(7)) comparator_8 (.a(in_1), .b(7'b0010111), .eq(out_9));  // open: gt, lt
  Comparator #(.width(7)) comparator_9 (.a(in_1), .b(7'b0110111), .eq(out_10));  // open: gt, lt

  // Notes on the sheet:
  //   R-TYPE
  //   JAL
  //   AND I
  //   LW
  //   JALR
  //   SW
  //   S
  //   BRANCH
  //   AUI PC
  //   LUI
endmodule

module NEXT_PC (
  input  BRANCH,
  input  JAL,
  input  JALR,
  output A,
  output B
);

  or or_1 (A, JAL, BRANCH);
  or or_2 (B, JALR, BRANCH);
endmodule

module IMMEDIATE_SELECTOR (
  input  STORE,
  input  UTYPE,
  input  ITYPE,
  output A,
  output B
);

  or or_1 (A, UTYPE, STORE);
  or or_2 (B, ITYPE, STORE);
endmodule

module ALUOP_O (
  input  RTYPE,
  input  ITYPE,
  input  LW,
  input  SW,
  input  JAL,
  input  JALR,
  input  LUI,
  input  ALUPC,
  output A,
  output B,
  output C
);

  or or_1 (A, ALUPC, LUI, JALR, JAL);
  or or_2 (B, ALUPC, LUI, SW, LW);
  or or_3 (C, ALUPC, JALR, SW, ITYPE);
endmodule

module ALU_CONTROL (
  input  ALUOP1,
  input  ALUOP2,
  input  ALUOP3,
  input  FUNC31,
  input  FUNC32,
  input  FUNC33,
  input  FUNC7,
  output A,
  output B,
  output C,
  output D
);

  wire and_1_out, and_2_out, and_3_out, and_4_out, and_5_out, and_6_out, and_7_out, and_8_out, and_9_out,
       and_10_out, and_11_out, and_12_out, and_13_out, and_14_out, and_15_out, and_16_out, and_17_out,
       not_1_out, not_2_out, not_3_out, not_4_out, not_5_out, not_6_out, not_7_out, not_8_out, not_9_out,
       not_10_out, not_11_out, not_12_out, not_13_out, not_14_out, not_15_out, not_16_out, not_17_out,
       not_18_out, not_19_out, not_20_out, not_21_out, not_22_out, not_23_out, not_24_out, not_25_out,
       not_26_out, not_27_out, not_28_out, not_29_out, not_30_out, not_31_out, not_32_out, not_33_out,
       not_34_out;

  not not_1 (not_1_out, ALUOP1);
  not not_2 (not_2_out, FUNC32);
  not not_3 (not_3_out, ALUOP1);
  not not_4 (not_4_out, FUNC31);
  not not_5 (not_5_out, ALUOP2);
  not not_6 (not_6_out, ALUOP1);
  not not_7 (not_7_out, FUNC31);
  not not_8 (not_8_out, FUNC32);
  not not_9 (not_9_out, ALUOP2);
  not not_10 (not_10_out, FUNC31);
  not not_11 (not_11_out, FUNC33);
  not not_12 (not_12_out, ALUOP1);
  not not_13 (not_13_out, FUNC32);
  not not_14 (not_14_out, FUNC33);
  not not_15 (not_15_out, ALUOP1);
  not not_16 (not_16_out, FUNC32);
  not not_17 (not_17_out, FUNC7);
  not not_18 (not_18_out, ALUOP2);
  not not_19 (not_19_out, ALUOP2);
  not not_20 (not_20_out, FUNC33);
  not not_21 (not_21_out, ALUOP1);
  not not_22 (not_22_out, FUNC7);
  not not_23 (not_23_out, ALUOP2);
  not not_24 (not_24_out, ALUOP2);
  not not_25 (not_25_out, ALUOP2);
  not not_26 (not_26_out, ALUOP3);
  not not_27 (not_27_out, ALUOP1);
  not not_28 (not_28_out, FUNC31);
  not not_29 (not_29_out, FUNC32);
  not not_30 (not_30_out, ALUOP1);
  not not_31 (not_31_out, FUNC32);
  not not_32 (not_32_out, ALUOP2);
  not not_33 (not_33_out, FUNC33);
  not not_34 (not_34_out, ALUOP2);
  and and_1 (and_1_out, not_1_out, not_2_out, FUNC33, FUNC7);
  and and_2 (and_2_out, not_3_out, not_4_out, FUNC32, FUNC33);
  and and_3 (and_3_out, ALUOP1, not_5_out);
  and and_4 (and_4_out, not_6_out, not_7_out, not_8_out, FUNC33);
  and and_5 (and_5_out, not_9_out, not_10_out, FUNC32, not_11_out);
  and and_6 (and_6_out, not_12_out, FUNC31, not_13_out, not_14_out);
  and and_7 (and_7_out, not_15_out, FUNC31, not_16_out, not_17_out);
  and and_8 (and_8_out, ALUOP1, not_18_out);
  and and_9 (and_9_out, not_19_out, FUNC32, not_20_out);
  and and_10 (and_10_out, not_21_out, FUNC31, FUNC33, not_22_out);
  and and_11 (and_11_out, not_23_out, FUNC31, FUNC32);
  and and_12 (and_12_out, ALUOP1, not_24_out);
  and and_13 (and_13_out, not_25_out, not_26_out, FUNC7);
  and and_14 (and_14_out, not_27_out, not_28_out, not_29_out, FUNC33);
  and and_15 (and_15_out, not_30_out, not_31_out, FUNC33, FUNC7);
  and and_16 (and_16_out, not_32_out, FUNC32, not_33_out);
  and and_17 (and_17_out, ALUOP1, not_34_out);
  or or_1 (A, and_1_out, and_2_out, and_3_out);
  or or_2 (B, and_4_out, and_5_out, and_6_out, and_7_out, and_8_out);
  or or_3 (C, and_9_out, and_10_out, and_11_out, and_12_out);
  or or_4 (D, and_13_out, and_14_out, and_15_out, and_16_out, and_17_out);
endmodule

module AL (
  input  [31:0] in_1,
  input  [31:0] in_2,
  input  [3:0] in_3,
  output [31:0] out_4
);

  wire comparator_1_lt, comparator_2_lt;
  wire [31:0] adder_1_out, and_1_out, bit_extender_1_out, bit_extender_2_out, or_1_out, shifter_1_out,
       shifter_2_out, shifter_3_out, subtractor_1_out, xor_1_out;

  IMMEDIATE_SELECTOR immediate_selector_1 ();  // open: STORE, UTYPE, ITYPE, A, B
  Adder #(.width(32)) adder_1 (.a(in_1), .b(in_2), .out(adder_1_out));  // open: cin, cout
  Subtractor #(.width(32)) subtractor_1 (.a(in_1), .b(in_2), .out(subtractor_1_out));  // open: bin, bout
  assign and_1_out = in_1 & in_2;  // AND_Gate and_1, 32 bits wide
  assign or_1_out = in_1 | in_2;  // OR_Gate or_1, 32 bits wide
  assign xor_1_out = in_1 ^ in_2;  // XOR_Gate xor_1, 32 bits wide
  Shifter #(.width(32)) shifter_1 (.in(in_1), .\dist (in_2[4:0]), .out(shifter_1_out));
  Shifter #(.width(32), .shift("lr")) shifter_2 (.in(in_1), .\dist (in_2[4:0]), .out(shifter_2_out));
  Comparator #(.width(32)) comparator_1 (.a(in_1), .b(in_2), .lt(comparator_1_lt));  // open: gt, eq
  assign bit_extender_1_out = {{31{comparator_1_lt}}, comparator_1_lt};  // Bit_Extender bit_extender_1
  assign bit_extender_2_out = {{31{1'b0}}, comparator_2_lt};  // Bit_Extender bit_extender_2
  Comparator #(.width(32)) comparator_2 (.a(in_2), .b(in_1), .lt(comparator_2_lt));  // open: gt, eq
  Shifter #(.width(32), .shift("ar")) shifter_3 (.in(in_1), .\dist (in_2[4:0]), .out(shifter_3_out));
  Multiplexer #(.select(4), .width(32)) multiplexer_1 (
    .in0(adder_1_out), .in1(subtractor_1_out), .in2(and_1_out), .in3(or_1_out), .in4(xor_1_out),
    .in5(shifter_1_out), .in6(shifter_2_out), .in7(bit_extender_1_out), .in8(bit_extender_2_out),
    .in9(shifter_3_out), .in15(in_1), .out(out_4), .sel(in_3));  // open: in10, in11, in12, in13, in14, en

  // Notes on the sheet:
  //   OPERAND A
  //   OPERAND B
endmodule

module CONTROLL (
  input  [6:0] in_1,
  input  [2:0] in_2,
  input  in_3,
  output out_4,
  output out_5,
  output out_6,
  output out_7,
  output [1:0] out_8,
  output out_9,
  output [1:0] out_10,
  output [3:0] out_11,
  output [1:0] out_12,
  output out_13
);

  wire type_decoder_1_out_2, type_decoder_1_out_3, type_decoder_1_out_4, type_decoder_1_out_5,
       type_decoder_1_out_6, type_decoder_1_out_7, type_decoder_1_out_8, type_decoder_1_out_9,
       type_decoder_1_out_10;

  TYPE_DECODER type_decoder_1 (
    .out_2(type_decoder_1_out_2), .out_3(type_decoder_1_out_3), .out_4(type_decoder_1_out_4),
    .out_5(type_decoder_1_out_5), .out_6(type_decoder_1_out_6), .out_7(type_decoder_1_out_7),
    .out_8(type_decoder_1_out_8), .out_9(type_decoder_1_out_9), .out_10(type_decoder_1_out_10), .in_1(in_1));
  DECODER decoder_1 (
    .I_type(type_decoder_1_out_2), .Load(type_decoder_1_out_4), .in_3(type_decoder_1_out_5),
    .Store(type_decoder_1_out_7), .Branch(type_decoder_1_out_8), .jal(type_decoder_1_out_3),
    .jalr(type_decoder_1_out_6), .lui(type_decoder_1_out_10), .Auipc(type_decoder_1_out_9), .in_10(in_2),
    .in_11(in_3), .REG_WRITE(out_4), .mem_to_reg(out_5), .MEM_WRITE(out_6), .BRANCH_2(out_7),
    .OPERAND_A(out_8), .OPERAND_B(out_9), .NEXT_PC(out_10), .out_20(out_11), .out_21(out_12), .out_17(out_13));
endmodule

module _32_register (
  input  [31:0] in_1,
  input  [4:0] in_2,
  input  in_3,
  input  [4:0] in_4,
  input  [4:0] in_5,
  input  in_6,
  output [31:0] out_7,
  output [31:0] out_8
);

  wire decoder_1_out0, decoder_1_out1, decoder_1_out2, decoder_1_out3, decoder_1_out4, decoder_1_out5,
       decoder_1_out6, decoder_1_out7, decoder_1_out8, decoder_1_out9, decoder_1_out10, decoder_1_out11,
       decoder_1_out12, decoder_1_out13, decoder_1_out14, decoder_1_out15, decoder_1_out16, decoder_1_out17,
       decoder_1_out18, decoder_1_out19, decoder_1_out20, decoder_1_out21, decoder_1_out22, decoder_1_out23,
       decoder_1_out24, decoder_1_out25, decoder_1_out26, decoder_1_out27, decoder_1_out28, decoder_1_out29,
       decoder_1_out30, decoder_1_out31, undriven;
  wire [31:0] register_1_q, register_2_q, register_3_q, register_4_q, register_5_q, register_6_q,
       register_7_q, register_8_q, register_9_q, register_10_q, register_11_q, register_12_q, register_13_q,
       register_14_q, register_15_q, register_16_q, register_17_q, register_18_q, register_19_q,
       register_20_q, register_21_q, register_22_q, register_23_q, register_24_q, register_25_q,
       register_26_q, register_27_q, register_28_q, register_29_q, register_30_q, register_31_q,
       register_32_q;

  Decoder #(.select(5)) decoder_1 (
    .out0(decoder_1_out0), .out1(decoder_1_out1), .out2(decoder_1_out2), .out3(decoder_1_out3),
    .out4(decoder_1_out4), .out5(decoder_1_out5), .out6(decoder_1_out6), .out7(decoder_1_out7),
    .out8(decoder_1_out8), .out9(decoder_1_out9), .out10(decoder_1_out10), .out11(decoder_1_out11),
    .out12(decoder_1_out12), .out13(decoder_1_out13), .out14(decoder_1_out14), .out15(decoder_1_out15),
    .out16(decoder_1_out16), .out17(decoder_1_out17), .out18(decoder_1_out18), .out19(decoder_1_out19),
    .out20(decoder_1_out20), .out21(decoder_1_out21), .out22(decoder_1_out22), .out23(decoder_1_out23),
    .out24(decoder_1_out24), .out25(decoder_1_out25), .out26(decoder_1_out26), .out27(decoder_1_out27),
    .out28(decoder_1_out28), .out29(decoder_1_out29), .out30(decoder_1_out30), .out31(decoder_1_out31),
    .sel(in_5), .en(in_3));
  Register #(.width(32)) register_1 (.D({32{1'b0}}), .en(decoder_1_out0), .Q(register_1_q), .clk(in_6));  // open: clr
  Register #(.width(32)) register_2 (.D(in_1), .en(decoder_1_out1), .Q(register_2_q), .clk(in_6));  // open: clr
  Register #(.width(32)) register_3 (.D(in_1), .en(decoder_1_out2), .Q(register_3_q), .clk(in_6));  // open: clr
  Register #(.width(32)) register_4 (.D(in_1), .en(decoder_1_out3), .Q(register_4_q), .clk(in_6));  // open: clr
  Register #(.width(32)) register_5 (.D(in_1), .en(decoder_1_out4), .Q(register_5_q), .clk(in_6));  // open: clr
  Register #(.width(32)) register_6 (.D(in_1), .en(decoder_1_out5), .Q(register_6_q), .clk(in_6));  // open: clr
  Register #(.width(32)) register_7 (.D(in_1), .en(decoder_1_out6), .Q(register_7_q), .clk(in_6));  // open: clr
  Register #(.width(32)) register_8 (.D(in_1), .en(decoder_1_out7), .Q(register_8_q), .clk(in_6));  // open: clr
  Register #(.width(32)) register_9 (.D(in_1), .en(decoder_1_out8), .Q(register_9_q), .clk(in_6));  // open: clr
  Register #(.width(32)) register_10 (.D(in_1), .en(decoder_1_out9), .Q(register_10_q), .clk(in_6));  // open: clr
  Register #(.width(32)) register_11 (.D(in_1), .en(decoder_1_out10), .Q(register_11_q), .clk(in_6));  // open: clr
  Register #(.width(32)) register_12 (.D(in_1), .en(decoder_1_out11), .Q(register_12_q), .clk(in_6));  // open: clr
  Register #(.width(32)) register_13 (.D(in_1), .en(decoder_1_out12), .Q(register_13_q), .clk(in_6));  // open: clr
  Register #(.width(32)) register_14 (.D(in_1), .en(decoder_1_out13), .Q(register_14_q), .clk(in_6));  // open: clr
  Register #(.width(32)) register_15 (.D(in_1), .en(decoder_1_out14), .Q(register_15_q), .clk(in_6));  // open: clr
  Register #(.width(32)) register_16 (.D(in_1), .en(decoder_1_out15), .Q(register_16_q), .clk(in_6));  // open: clr
  Register #(.width(32)) register_17 (.D(in_1), .en(decoder_1_out16), .Q(register_17_q), .clk(in_6));  // open: clr
  Register #(.width(32)) register_18 (.D(in_1), .en(decoder_1_out17), .Q(register_18_q), .clk(in_6));  // open: clr
  Register #(.width(32)) register_19 (.D(in_1), .en(decoder_1_out18), .Q(register_19_q), .clk(in_6));  // open: clr
  Register #(.width(32)) register_20 (.D(in_1), .en(decoder_1_out19), .Q(register_20_q), .clk(in_6));  // open: clr
  Register #(.width(32)) register_21 (.D(in_1), .en(decoder_1_out20), .Q(register_21_q), .clk(in_6));  // open: clr
  Register #(.width(32)) register_22 (.D(in_1), .en(decoder_1_out21), .Q(register_22_q), .clk(in_6));  // open: clr
  Register #(.width(32)) register_23 (.D(in_1), .en(decoder_1_out22), .Q(register_23_q), .clk(in_6));  // open: clr
  Register #(.width(32)) register_24 (.D(in_1), .en(decoder_1_out23), .Q(register_24_q), .clk(in_6));  // open: clr
  Register #(.width(32)) register_25 (.D(in_1), .en(decoder_1_out24), .Q(register_25_q), .clk(in_6));  // open: clr
  Register #(.width(32)) register_26 (.D(in_1), .en(decoder_1_out25), .Q(register_26_q), .clk(in_6));  // open: clr
  Register #(.width(32)) register_27 (.D(in_1), .en(decoder_1_out26), .Q(register_27_q), .clk(in_6));  // open: clr
  Register #(.width(32)) register_28 (.D(in_1), .en(decoder_1_out27), .Q(register_28_q), .clk(in_6));  // open: clr
  Register #(.width(32)) register_29 (.D(in_1), .en(decoder_1_out28), .Q(register_29_q), .clk(in_6));  // open: clr
  Register #(.width(32)) register_30 (.D(in_1), .en(decoder_1_out29), .Q(register_30_q), .clk(in_6));  // open: clr
  Register #(.width(32)) register_31 (.D(in_1), .en(decoder_1_out30), .Q(register_31_q), .clk(in_6));  // open: clr
  Register #(.width(32)) register_32 (.D(in_1), .en(decoder_1_out31), .Q(register_32_q), .clk(in_6));  // open: clr
  Multiplexer #(.select(5), .width(32)) multiplexer_1 (
    .in0(register_1_q), .in1(register_2_q), .in2(register_3_q), .in3(register_4_q), .in4(register_5_q),
    .in5(register_6_q), .in6(register_7_q), .in7(register_8_q), .in8(register_9_q), .in9(register_10_q),
    .in10(register_11_q), .in11(register_12_q), .in12(register_13_q), .in13(register_14_q),
    .in14(register_15_q), .in15(register_16_q), .in16(register_17_q), .in17(register_18_q),
    .in18(register_19_q), .in19(register_20_q), .in20(register_21_q), .in21(register_22_q),
    .in22(register_23_q), .in23(register_24_q), .in24(register_25_q), .in25(register_26_q),
    .in26(register_27_q), .in27(register_28_q), .in28(register_29_q), .in29(register_30_q),
    .in30(register_31_q), .in31(register_32_q), .out(out_7), .sel(in_2), .en(undriven));
  Multiplexer #(.select(5), .width(32)) multiplexer_2 (
    .in0(register_1_q), .in1(register_2_q), .in2(register_3_q), .in3(register_4_q), .in4(register_5_q),
    .in5(register_6_q), .in6(register_7_q), .in7(register_8_q), .in8(register_9_q), .in9(register_10_q),
    .in10(register_11_q), .in11(register_12_q), .in12(register_13_q), .in13(register_14_q),
    .in14(register_15_q), .in15(register_16_q), .in16(register_17_q), .in17(register_18_q),
    .in18(register_19_q), .in19(register_20_q), .in20(register_21_q), .in21(register_22_q),
    .in22(register_23_q), .in23(register_24_q), .in24(register_25_q), .in25(register_26_q),
    .in26(register_27_q), .in27(register_28_q), .in28(register_29_q), .in29(register_30_q),
    .in30(register_31_q), .in31(register_32_q), .out(out_8), .sel(in_4));  // open: en
endmodule

module BRANCH (
  input  [31:0] in_1,
  input  [31:0] in_2,
  input  [2:0] in_3,
  input  in_4,
  output out_5
);

  wire comparator_1_eq, comparator_2_eq, comparator_3_lt, comparator_4_eq, comparator_4_gt, comparator_5_lt,
       comparator_6_eq, comparator_6_gt, not_1_out, or_1_out, or_2_out;

  Comparator #(.width(32)) comparator_1 (.a(in_1), .b(in_2), .eq(comparator_1_eq));  // open: gt, lt
  Comparator #(.width(32)) comparator_2 (.a(in_1), .b(in_2), .eq(comparator_2_eq));  // open: gt, lt
  Comparator #(.width(32)) comparator_3 (.a(in_1), .b(in_2), .lt(comparator_3_lt));  // open: gt, eq
  Comparator #(.width(32)) comparator_4 (.a(in_1), .b(in_2), .gt(comparator_4_gt), .eq(comparator_4_eq));  // open: lt
  Comparator #(.width(32), .mode("unsigned")) comparator_5 (.a(in_1), .b(in_2), .lt(comparator_5_lt));  // open: gt, eq
  Comparator #(.width(32), .mode("unsigned")) comparator_6 (
    .a(in_1), .b(in_2), .gt(comparator_6_gt), .eq(comparator_6_eq));  // open: lt
  not not_1 (not_1_out, comparator_2_eq);
  or or_1 (or_1_out, comparator_4_eq, comparator_4_gt);
  or or_2 (or_2_out, comparator_6_gt, comparator_6_eq);
  Multiplexer #(.select(3)) multiplexer_1 (
    .in0(comparator_1_eq), .in1(not_1_out), .in4(comparator_3_lt), .in5(or_1_out), .in6(comparator_5_lt),
    .in7(or_2_out), .out(out_5), .sel(in_3), .en(in_4));  // open: in2, in3

  // Notes on the sheet:
  //   BEQ
  //   BNE
  //   BLT
  //   BGE
  //   BLTU
  //   BGEU
endmodule

module OPA (
  input  AUIPC,
  input  JAL,
  input  JALR,
  input  LUI,
  input  RS1,
  output A,
  output B
);

  or or_1 (A, LUI, AUIPC);
  or or_2 (B, LUI, JALR, JAL);
endmodule

module DECODER (
  input  I_type,
  input  Load,
  input  in_3,
  input  Store,
  input  Branch,
  input  jal,
  input  jalr,
  input  lui,
  input  Auipc,
  input  [2:0] in_10,
  input  in_11,
  output REG_WRITE,
  output mem_to_reg,
  output MEM_WRITE,
  output BRANCH_2,
  output [1:0] OPERAND_A,
  output out_17,
  output OPERAND_B,
  output [1:0] NEXT_PC,
  output [3:0] out_20,
  output [1:0] out_21
);

  wire aluop_o_1_a, aluop_o_1_b, aluop_o_1_c, or_1_out, or_2_out;

  or or_1 (or_1_out, Auipc, lui);
  or or_2 (or_2_out, jalr, in_3, Load);
  or or_3 (REG_WRITE, I_type, Load, in_3, Auipc, jal, jalr, lui);
  OPA opa_1 (.AUIPC(Auipc), .JAL(jal), .JALR(jalr), .LUI(lui), .A(OPERAND_A[0]), .B(OPERAND_A[1]));  // open: RS1
  or or_4 (OPERAND_B, Auipc, Store, lui, Branch, Load);
  NEXT_PC next_pc_1 (.BRANCH(Branch), .JAL(jal), .JALR(jalr), .A(NEXT_PC[1]), .B(NEXT_PC[0]));
  ALUOP_O aluop_o_1 (
    .RTYPE(I_type), .ITYPE(Load), .LW(in_3), .SW(Store), .JAL(jal), .JALR(jalr), .LUI(lui), .ALUPC(Auipc),
    .A(aluop_o_1_a), .B(aluop_o_1_b), .C(aluop_o_1_c));
  IMMEDIATE_SELECTOR immediate_selector_1 (
    .STORE(Store), .UTYPE(or_1_out), .ITYPE(or_2_out), .A(out_21[0]), .B(out_21[1]));
  ALU_CONTROL alu_control_1 (
    .ALUOP1(aluop_o_1_a), .ALUOP2(aluop_o_1_b), .ALUOP3(aluop_o_1_c), .FUNC31(in_10[2]), .FUNC32(in_10[1]),
    .FUNC33(in_10[0]), .FUNC7(in_11), .A(out_20[3]), .B(out_20[2]), .C(out_20[1]), .D(out_20[0]));

  assign BRANCH_2 = Branch;
  assign mem_to_reg = in_3;
  assign MEM_WRITE = Store;
  assign out_17 = in_3;

  // Notes on the sheet:
  //   R-type
  //   Immegiate-selector
  //   ALU_CONTROL
endmodule

module single_cycle (
  output [31:0] out_1,
  output out_2,
  output [1:0] out_3,
  output [1:0] out_4,
  output out_5,
  output [31:0] out_6
);

  wire branch_1_out_5, controll_1_out_4, controll_1_out_5, e, h;
  wire [1:0] controll_1_out_12;
  wire [3:0] controll_1_out_11;
  wire [11:0] register_1_q_2;
  wire [31:0] adder_1_out, adder_2_out, b, immegiate_generation_1_out_3, immegiate_generation_1_out_4,
       immegiate_generation_1_out_5, immegiate_generation_1_out_6, immegiate_generation_1_out_7,
       multiplexer_1_out, multiplexer_2_out, multiplexer_3_out, multiplexer_4_out, multiplexer_5_out,
       multiplexer_6_out, ram_1_data, register_1_q, rom_1_data;

  Adder #(.width(32)) adder_1 (.a(out_1), .b(immegiate_generation_1_out_3), .out(adder_1_out));  // open: cin, cout
  Clock clock_1 (.out(h));
  Multiplexer #(.select(2), .width(32), .enable("false")) multiplexer_1 (
    .in0(adder_2_out), .in1(adder_1_out), .in2(immegiate_generation_1_out_6), .in3(multiplexer_2_out),
    .out(multiplexer_1_out), .sel(out_3));
  Multiplexer #(.width(32), .enable("false")) multiplexer_2 (
    .in0(adder_2_out), .in1(immegiate_generation_1_out_5), .out(multiplexer_2_out), .sel(branch_1_out_5));
  Register #(.width(32)) register_1 (
    .D(multiplexer_1_out), .Q({register_1_q[31:14], register_1_q_2, register_1_q[1:0]}), .clk(h));  // open: en, clr
  Adder #(.width(32)) adder_2 (
    .a({register_1_q[31:14], register_1_q_2, register_1_q[1:0]}), .b(32'h4), .out(adder_2_out));  // open: cin, cout
  BRANCH branch_1 (.in_1(out_1), .in_2(b), .out_5(branch_1_out_5), .in_3(rom_1_data[14:12]), .in_4(e));
  ROM #(.addrWidth(12), .dataWidth(32)) rom_1 (.addr(register_1_q_2), .data(rom_1_data));  // open: sel
  immegiate_generation immegiate_generation_1 (
    .in_1({register_1_q[31:14], register_1_q_2, register_1_q[1:0]}), .in_2(rom_1_data),
    .out_3(immegiate_generation_1_out_3), .out_4(immegiate_generation_1_out_4),
    .out_5(immegiate_generation_1_out_5), .out_6(immegiate_generation_1_out_6),
    .out_7(immegiate_generation_1_out_7));
  CONTROLL controll_1 (
    .out_4(controll_1_out_4), .in_1(rom_1_data[6:0]), .in_3(rom_1_data[30]), .in_2(rom_1_data[14:12]),
    .out_6(out_2), .out_7(e), .out_5(controll_1_out_5), .out_8(out_4), .out_9(out_5), .out_10(out_3),
    .out_12(controll_1_out_12), .out_11(controll_1_out_11), .out_13(controll_1_out_5));
  Multiplexer #(.select(2), .width(32), .enable("false")) multiplexer_3 (
    .in1(immegiate_generation_1_out_7), .in2(immegiate_generation_1_out_3),
    .in3(immegiate_generation_1_out_4), .out(multiplexer_3_out), .sel(controll_1_out_12));  // open: in0
  _32_register u_32_register_1 (
    .in_1(multiplexer_6_out), .in_2(rom_1_data[19:15]), .in_3(controll_1_out_4), .in_4(rom_1_data[24:20]),
    .in_5(rom_1_data[11:7]), .in_6(h), .out_7(out_1), .out_8(b));
  Multiplexer #(.select(2), .width(32), .enable("false")) multiplexer_4 (
    .in0(out_1), .in1({register_1_q[31:14], register_1_q_2, register_1_q[1:0]}), .in2(adder_2_out),
    .in3({32{1'b0}}), .out(multiplexer_4_out), .sel(out_4));
  Multiplexer #(.width(32), .enable("false")) multiplexer_5 (
    .in0(b), .in1(multiplexer_3_out), .out(multiplexer_5_out), .sel(out_5));
  AL al_1 (.in_1(multiplexer_4_out), .in_2(multiplexer_5_out), .in_3(controll_1_out_11), .out_4(out_6));
  RAM #(.addrWidth(12), .dataWidth(32), .bus("separate")) ram_1 (
    .addr(out_6[13:2]), .din(b), .data(ram_1_data), .str(out_2), .clk(h), .ld(controll_1_out_5));  // open: sel, clr
  Multiplexer #(.width(32)) multiplexer_6 (
    .in0(out_6), .in1(ram_1_data), .out(multiplexer_6_out), .sel(controll_1_out_5));  // open: en

  // Other names for the same wires on the sheet: a[31:0] = out_1; f[1:0] = out_3

  // Notes on the sheet:
  //   contents of rom_1 (hex, n*v repeats v):
  //   500313 a00393 3200e13 530313 1c30463 ff9ff0ef
endmodule
